// Logisim project circuito.circ as structural Verilog: 6 circuits, main circuit main
module main (
  input  [7:0] in_1,
  input  [7:0] in_2
);

  wire aa, ab, ac, ad, ae, af, ag, ba, bb, bc, bd, be, bf, bg, ca, cb, cc, cd, ce, cf, cg, da, db, dc, dd,
       de, df, dg, ea, eb, ec, ed, ee, ef, eg, fa, fb, fc, fd, fe, ff, fg, S_V_1_S, S_V_2_S;
  wire [3:0] view_number_1_centenas, view_number_1_decenas, view_number_1_unidades, view_number_2_centenas,
       view_number_2_decenas, view_number_2_unidades;

  _7_Segment_Display u_7_segment_display_1 (.g(S_V_1_S));  // open: f, a, b, e, d, c, dp
  _7_Segment_Display u_7_segment_display_2 (.g(ag), .f(af), .a(aa), .b(ab), .e(ae), .d(ad), .c(ac));  // open: dp
  _7_Segment_Display u_7_segment_display_3 (.g(bg), .f(bf), .a(ba), .b(bb), .e(be), .d(bd), .c(bc));  // open: dp
  _7_Segment_Display u_7_segment_display_4 (.g(cg), .f(cf), .a(ca), .b(cb), .e(ce), .d(cd), .c(cc));  // open: dp
  _7_Segment_Display u_7_segment_display_5 (.g(S_V_2_S));  // open: f, a, b, e, d, c, dp
  _7_Segment_Display u_7_segment_display_6 (.g(dg), .f(df), .a(da), .b(db), .e(de), .d(dd), .c(dc));  // open: dp
  _7_Segment_Display u_7_segment_display_7 (.g(eg), .f(ef), .a(ea), .b(eb), .e(ee), .d(ed), .c(ec));  // open: dp
  vector vector_1 ();  // open: numero_entrada, posicion_entrada, reset, reloj, posicion_salida, salida_posicion_1, salida_posicion_2
  _7_Segment_Display u_7_segment_display_8 (.g(fg), .f(ff), .a(fa), .b(fb), .e(fe), .d(fd), .c(fc));  // open: dp
  view_number view_number_1 (
    .in_1(in_1), .Signo(S_V_1_S), .centenas(view_number_1_centenas), .Decenas(view_number_1_decenas),
    .Unidades(view_number_1_unidades));
  deco_segmento deco_segmento_1 (
    .numero(view_number_1_centenas), .a(aa), .b(ab), .c(ac), .d(ad), .e(ae), .f(af), .g(ag));
  deco_segmento deco_segmento_2 (
    .numero(view_number_1_unidades), .a(ca), .b(cb), .c(cc), .d(cd), .e(ce), .f(cf), .g(cg));
  deco_segmento deco_segmento_3 (
    .numero(view_number_1_decenas), .a(ba), .b(bb), .c(bc), .d(bd), .e(be), .f(bf), .g(bg));
  view_number view_number_2 (
    .in_1(in_2), .Signo(S_V_2_S), .centenas(view_number_2_centenas), .Decenas(view_number_2_decenas),
    .Unidades(view_number_2_unidades));
  deco_segmento deco_segmento_4 (
    .numero(view_number_2_centenas), .a(da), .b(db), .c(dc), .d(dd), .e(de), .f(df), .g(dg));
  deco_segmento deco_segmento_5 (
    .numero(view_number_2_unidades), .a(fa), .b(fb), .c(fc), .d(fd), .e(fe), .f(ff), .g(fg));
  deco_segmento deco_segmento_6 (
    .numero(view_number_2_decenas), .a(ea), .b(eb), .c(ec), .d(ed), .e(ee), .f(ef), .g(eg));

  // Other names for the same wires on the sheet: S_V_1[7:0] = in_1; S_V_2[7:0] = in_2

  // Notes on the sheet:
  //   Numero a del vector
  //   Numero a+1 del vector
endmodule

module arreglo_8bits (
  input  [7:0] numero_entrada,
  input  reset,
  input  reloj,
  output [7:0] numero_salida
);

  wire j_k_ff_1_qn, j_k_ff_2_qn, j_k_ff_3_qn, j_k_ff_4_qn, j_k_ff_5_qn, j_k_ff_6_qn, j_k_ff_7_qn, j_k_ff_8_qn;

  J_K_Flip_Flop j_k_ff_1 (
    .J(numero_entrada[7]), .K(j_k_ff_1_qn), .clk(reloj), .Q(numero_salida[7]), .Qn(j_k_ff_1_qn), .reset(reset));  // open: preset
  J_K_Flip_Flop j_k_ff_2 (
    .J(numero_entrada[6]), .K(j_k_ff_2_qn), .clk(reloj), .Q(numero_salida[6]), .Qn(j_k_ff_2_qn), .reset(reset));  // open: preset
  J_K_Flip_Flop j_k_ff_3 (
    .J(numero_entrada[5]), .K(j_k_ff_3_qn), .clk(reloj), .Q(numero_salida[5]), .Qn(j_k_ff_3_qn), .reset(reset));  // open: preset
  J_K_Flip_Flop j_k_ff_4 (
    .J(numero_entrada[4]), .K(j_k_ff_4_qn), .clk(reloj), .Q(numero_salida[4]), .Qn(j_k_ff_4_qn), .reset(reset));  // open: preset
  J_K_Flip_Flop j_k_ff_5 (
    .J(numero_entrada[3]), .K(j_k_ff_5_qn), .clk(reloj), .Q(numero_salida[3]), .Qn(j_k_ff_5_qn), .reset(reset));  // open: preset
  J_K_Flip_Flop j_k_ff_6 (
    .J(numero_entrada[2]), .K(j_k_ff_6_qn), .clk(reloj), .Q(numero_salida[2]), .Qn(j_k_ff_6_qn), .reset(reset));  // open: preset
  J_K_Flip_Flop j_k_ff_7 (
    .J(numero_entrada[1]), .K(j_k_ff_7_qn), .clk(reloj), .Q(numero_salida[1]), .Qn(j_k_ff_7_qn), .reset(reset));  // open: preset
  J_K_Flip_Flop j_k_ff_8 (
    .J(numero_entrada[0]), .K(j_k_ff_8_qn), .clk(reloj), .Q(numero_salida[0]), .Qn(j_k_ff_8_qn), .reset(reset));  // open: preset
endmodule

module vector (
  input  [7:0] numero_entrada,
  input  [3:0] posicion_entrada,
  input  reset,
  input  reloj,
  input  [3:0] posicion_salida,
  output [7:0] salida_posicion_1,
  output [7:0] salida_posicion_2
);

  wire [3:0] adder_1_out;
  wire [7:0] demultiplexer_1_out0, demultiplexer_1_out1, demultiplexer_1_out2, demultiplexer_1_out3,
       demultiplexer_1_out4, demultiplexer_1_out5, demultiplexer_1_out6, demultiplexer_1_out7,
       demultiplexer_1_out8, demultiplexer_1_out9, demultiplexer_1_out10, demultiplexer_1_out11,
       demultiplexer_1_out12, demultiplexer_1_out13, demultiplexer_1_out14, demultiplexer_1_out15,
       position_0_numero_salida, position_1_numero_salida, position_2_numero_salida,
       position_3_numero_salida, position_4_numero_salida, position_5_numero_salida,
       position_6_numero_salida, position_7_numero_salida, position_8_numero_salida,
       position_9_numero_salida, position_10_numero_salida, position_11_numero_salida,
       position_12_numero_salida, position_13_numero_salida, position_14_numero_salida,
       position_15_numero_salida;

  Demultiplexer #(.select(4), .width(8)) demultiplexer_1 (
    .out0(demultiplexer_1_out0), .out1(demultiplexer_1_out1), .out2(demultiplexer_1_out2),
    .out3(demultiplexer_1_out3), .out4(demultiplexer_1_out4), .out5(demultiplexer_1_out5),
    .out6(demultiplexer_1_out6), .out7(demultiplexer_1_out7), .out8(demultiplexer_1_out8),
    .out9(demultiplexer_1_out9), .out10(demultiplexer_1_out10), .out11(demultiplexer_1_out11),
    .out12(demultiplexer_1_out12), .out13(demultiplexer_1_out13), .out14(demultiplexer_1_out14),
    .out15(demultiplexer_1_out15), .in(numero_entrada), .sel(posicion_entrada));
  arreglo_8bits position_0 (
    .numero_entrada(demultiplexer_1_out0), .reset(reset), .reloj(reloj),
    .numero_salida(position_0_numero_salida));
  arreglo_8bits position_1 (
    .numero_entrada(demultiplexer_1_out1), .reset(reset), .reloj(reloj),
    .numero_salida(position_1_numero_salida));
  arreglo_8bits position_2 (
    .numero_entrada(demultiplexer_1_out2), .reset(reset), .reloj(reloj),
    .numero_salida(position_2_numero_salida));
  arreglo_8bits position_3 (
    .numero_entrada(demultiplexer_1_out3), .reset(reset), .reloj(reloj),
    .numero_salida(position_3_numero_salida));
  arreglo_8bits position_4 (
    .numero_entrada(demultiplexer_1_out4), .reset(reset), .reloj(reloj),
    .numero_salida(position_4_numero_salida));
  arreglo_8bits position_5 (
    .numero_entrada(demultiplexer_1_out5), .reset(reset), .reloj(reloj),
    .numero_salida(position_5_numero_salida));
  arreglo_8bits position_6 (
    .numero_entrada(demultiplexer_1_out6), .reset(reset), .reloj(reloj),
    .numero_salida(position_6_numero_salida));
  arreglo_8bits position_7 (
    .numero_entrada(demultiplexer_1_out7), .reset(reset), .reloj(reloj),
    .numero_salida(position_7_numero_salida));
  arreglo_8bits position_8 (
    .numero_entrada(demultiplexer_1_out8), .reset(reset), .reloj(reloj),
    .numero_salida(position_8_numero_salida));
  arreglo_8bits position_9 (
    .numero_entrada(demultiplexer_1_out9), .reset(reset), .reloj(reloj),
    .numero_salida(position_9_numero_salida));
  arreglo_8bits position_10 (
    .numero_entrada(demultiplexer_1_out10), .reset(reset), .reloj(reloj),
    .numero_salida(position_10_numero_salida));
  arreglo_8bits position_11 (
    .numero_entrada(demultiplexer_1_out11), .reset(reset), .reloj(reloj),
    .numero_salida(position_11_numero_salida));
  arreglo_8bits position_12 (
    .numero_entrada(demultiplexer_1_out12), .reset(reset), .reloj(reloj),
    .numero_salida(position_12_numero_salida));
  arreglo_8bits position_13 (
    .numero_entrada(demultiplexer_1_out13), .reset(reset), .reloj(reloj),
    .numero_salida(position_13_numero_salida));
  arreglo_8bits position_14 (
    .numero_entrada(demultiplexer_1_out14), .reset(reset), .reloj(reloj),
    .numero_salida(position_14_numero_salida));
  arreglo_8bits position_15 (
    .numero_entrada(demultiplexer_1_out15), .reset(reset), .reloj(reloj),
    .numero_salida(position_15_numero_salida));
  Adder #(.width(4)) adder_1 (.a(posicion_salida), .b(4'b0001), .out(adder_1_out));  // open: cin, cout
  Multiplexer #(.select(4), .width(8)) multiplexer_1 (
    .in0(position_0_numero_salida), .in1(position_1_numero_salida), .in2(position_2_numero_salida),
    .in3(position_3_numero_salida), .in4(position_4_numero_salida), .in5(position_5_numero_salida),
    .in6(position_6_numero_salida), .in7(position_7_numero_salida), .in8(position_8_numero_salida),
    .in9(position_9_numero_salida), .in10(position_10_numero_salida), .in11(position_11_numero_salida),
    .in12(position_12_numero_salida), .in13(position_13_numero_salida), .in14(position_14_numero_salida),
    .in15(position_15_numero_salida), .out(salida_posicion_1), .sel(posicion_salida));
  Multiplexer #(.select(4), .width(8)) multiplexer_2 (
    .in0(position_0_numero_salida), .in1(position_1_numero_salida), .in2(position_2_numero_salida),
    .in3(position_3_numero_salida), .in4(position_4_numero_salida), .in5(position_5_numero_salida),
    .in6(position_6_numero_salida), .in7(position_7_numero_salida), .in8(position_8_numero_salida),
    .in9(position_9_numero_salida), .in10(position_10_numero_salida), .in11(position_11_numero_salida),
    .in12(position_12_numero_salida), .in13(position_13_numero_salida), .in14(position_14_numero_salida),
    .in15(position_15_numero_salida), .out(salida_posicion_2), .sel(adder_1_out));
endmodule

module deco_segmento (
  input  [3:0] numero,
  output a,
  output b,
  output c,
  output d,
  output e,
  output f,
  output g
);

  wire and_1_out, and_2_out, and_3_out, and_4_out, and_5_out, and_6_out, and_7_out, and_8_out, and_9_out,
       and_10_out, and_11_out, and_12_out, and_13_out, and_14_out, and_15_out, and_16_out, not_1_out,
       not_2_out, not_3_out;

  not not_1 (not_1_out, numero[2]);
  not not_2 (not_2_out, numero[1]);
  not not_3 (not_3_out, numero[0]);
  and and_1 (and_1_out, not_1_out, not_3_out);
  and and_2 (and_2_out, numero[2], numero[0]);
  and and_3 (and_3_out, not_2_out, not_3_out);
  and and_4 (and_4_out, numero[1], numero[0]);
  or or_1 (c, not_2_out, numero[0], numero[2]);
  and and_5 (and_5_out, not_1_out, not_3_out);
  and and_6 (and_6_out, not_1_out, numero[1]);
  and and_7 (and_7_out, numero[1], not_3_out);
  and and_8 (and_8_out, numero[2], not_2_out, numero[0]);
  and and_9 (and_9_out, not_1_out, not_3_out);
  and and_10 (and_10_out, numero[1], not_3_out);
  and and_11 (and_11_out, not_2_out, not_3_out);
  and and_12 (and_12_out, numero[2], not_2_out);
  and and_13 (and_13_out, numero[2], not_3_out);
  and and_14 (and_14_out, not_1_out, numero[1]);
  and and_15 (and_15_out, numero[2], not_2_out);
  and and_16 (and_16_out, numero[2], not_3_out);
  or or_2 (a, and_1_out, numero[1], and_2_out, numero[3]);
  or or_3 (b, not_1_out, and_3_out, and_4_out);
  or or_4 (d, and_5_out, and_6_out, and_7_out, and_8_out, numero[3]);
  or or_5 (e, and_9_out, and_10_out);
  or or_6 (f, and_11_out, and_12_out, and_13_out, numero[3]);
  or or_7 (g, and_14_out, and_15_out, and_16_out, numero[3]);
endmodule

module complemento_2 (
  input  [7:0] Entrada_numero,
  output [7:0] Salida_complemento
);

  wire [7:0] xor_1_out;

  xor xor_1 (xor_1_out[0], Entrada_numero[0], Entrada_numero[7]);
  xor xor_2 (xor_1_out[1], Entrada_numero[1], Entrada_numero[7]);
  xor xor_3 (xor_1_out[2], Entrada_numero[2], Entrada_numero[7]);
  xor xor_4 (xor_1_out[3], Entrada_numero[3], Entrada_numero[7]);
  xor xor_5 (xor_1_out[4], Entrada_numero[4], Entrada_numero[7]);
  xor xor_6 (xor_1_out[5], Entrada_numero[5], Entrada_numero[7]);
  xor xor_7 (xor_1_out[6], Entrada_numero[6], Entrada_numero[7]);
  xor xor_8 (xor_1_out[7], Entrada_numero[7], Entrada_numero[7]);
  Adder adder_1 (.a(xor_1_out), .b({8{1'b0}}), .out(Salida_complemento), .cin(Entrada_numero[7]));  // open: cout
endmodule

module view_number (
  input  [7:0] in_1,
  output Signo,
  output [3:0] centenas,
  output [3:0] Decenas,
  output [3:0] Unidades
);

  wire [7:0] complemento_2_1_salida_complemento, divider_1_out, divider_1_rem, divider_2_out, divider_2_rem;

  BitSelector bitselector_1 (.in(in_1), .out(Signo), .sel(3'b111));
  complemento_2 complemento_2_1 (.Entrada_numero(in_1), .Salida_complemento(complemento_2_1_salida_complemento));
  Divider divider_1 (
    .a(complemento_2_1_salida_complemento), .b(8'ha), .out(divider_1_out), .rem(divider_1_rem));  // open: upper
  Divider divider_2 (.a(divider_1_out), .b(8'ha), .out(divider_2_out), .rem(divider_2_rem));  // open: upper
  Bit_Extender #(.out_width(4)) bit_extender_1 (.in(divider_2_out), .out(centenas));
  Bit_Extender #(.out_width(4)) bit_extender_2 (.in(divider_2_rem), .out(Decenas));
  Bit_Extender #(.out_width(4)) bit_extender_3 (.in(divider_1_rem), .out(Unidades));
endmodule
